# Fritzing sketch Car_circuit (saved by Fritzing 0.9.4)
breadboards: 1

parts:
  VCC1 = Battery
  S2 = Toggle Switch [package=THT]
  U3 = LM2596 step down module
  VCC2 = Battery  # not connected
  L298N1 = L298N DC motor driver
  M1 = Getriebemotor
  M2 = Getriebemotor
  Part5 = Arduino Uno (Rev3)
  Part6 = Bluetooth HC-05 Macho
  YwRobot_Power_Supply1 = YwRobot Breadboard Power Supply [part_number=545043]

nets:
  N1: VCC1.+, S2.L1
  N2: S2.COM, U3.IN+
  N3: U3.OUT+, L298N1.12V
  N4: U3.OUT-, L298N1.GND
  N5: L298N1.OUT1, M1.pin_2
  N6: L298N1.OUT2, M1.pin_1
  N7: L298N1.OUT3, M2.pin_2
  N8: L298N1.OUT4, M2.pin_1
  N9: L298N1.ENA, Part5.D5_PWM
  N10: L298N1.ENB, Part5.D6_PWM
  N11: L298N1.IN1, Part5.D3_PWM
  N12: L298N1.IN2, Part5.D4
  N13: L298N1.IN3, Part5.D8
  N14: L298N1.IN4, Part5.D7
  N15: Part5.D10_PWM/SS, Part6.TXD
  N16: Part5.D11_PWM/MOSI, Part6.RXD
  GND: Part5.GND, Part6.GND, YwRobot_Power_Supply1.GND
  5V: Part5.5V, Part6.VCC
  VIN: Part5.VIN, YwRobot_Power_Supply1.VCC

custom parts:
  LM2596 step down module: LM2596 DC-DC step down power supply module 3 A.
  L298N DC motor driver: 2x DC motor driver with 78M05 positive voltage regulator (7..35 V) L298N: max 46 V, 2 A Set 5 V Enable jumper to enable 5 V regultor (needed for the L298N) and +5 V output at screw terminal or supply external +5 V at screw terminal Set ENA and/or ENB to +5 V to enable motor permanently or supply ENA and/or ENB with PWM signal IN1 and IN2 set rotation directory for motor A (OUT1/OUT2) IN2 and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
  YwRobot Breadboard Power Supply: The YwRobot Breadboard Power Supply (MB-V2) has two power rails; they can be 5V or 3V3. Power to the module can be provided through the female USB socket or through the A10 (female) 2.1mm power jack.
