# Fritzing sketch Car_control_joystick (saved by Fritzing 0.9.4)
breadboards: 1

parts:
  Part1 = Arduino Mega 2560 (Rev3)
  Part2 = Bluetooth HC-05 Macho
  U1 = POT [package=alps_pot]  # not connected
  Part4 = Black Joystick KY-023
  R1 = Resistor [tolerance=±5% resistance=220 package="0805 [SMD]"]

nets:
  N1: Part1.A0, Part4.VRx
  N2: Part1.A1, Part4.VRy
  N3: Part1.D11_PWM, Part2.RXD
  N4: Part1.D10_PWM, Part2.TXD
  N5: Part1.D9_PWM, R1.Pin_1
  5V: Part1.5V, Part4.+5V
  GND: Part1.GND, Part4.GND
  N6: Part4.SW, R1.Pin_0

custom parts:
  Black Joystick KY-023: Description: The joystick is a combination of 2 analoog potentiometer and a digital switch. Arduino GND --> Module pin - Arduino +5V --> Module pin +5V Arduino Analoog 0 --> Module VRx Arduino Analoog 1 --> Module VRy Arduino Digital --> Module SW Dimensions: 1" x 1.25"
